# Fritzing sketch arduino_micromanipulator (saved by Fritzing 0.9.2b)
breadboards: 1

parts:
  Part1 = Arduino Uno (Rev3)
  Part2 = Thumb Joystick
  M2 = DC Motor
  V1 = DC Power [voltage=5]
  V2 = DC Power [voltage=12V]
  M1 = DC Motor
  U1 = mystery part, 14 pins [chip_label="Critical Velocity H-Bridge"]

nets:
  N1: Part1.A0, Part2.VERT
  N2: Part1.A1, Part2.HORZ
  N3: Part1.D8, Part2.SEL
  N4: Part1.D2, U1.pin2
  N5: Part1.D3_PWM, U1.pin3
  N6: Part1.D4, U1.pin6
  N7: Part1.D5_PWM, U1.pin7
  5V: Part1.5V, Part2.VCC, V1.V+, U1.pin1, U1.pin5
  GND: Part1.GND, Part2.GND, V1.V-, U1.pin4, U1.pin8
  N8: M2.pin_1, U1.pin13
  N9: M2.pin_2, U1.pin14
  N10: V2.V+, U1.pin9
  N11: V2.V-, U1.pin10
  N12: M1.pin_1, U1.pin11
  N13: M1.pin_2, U1.pin12
